// Logisim project Trabalho4Zeq.circ as structural Verilog: 9 circuits, main circuit main
module main (
  input  Clock,
  input  Clear,
  output [31:0] out_3
);

  wire alu_1_zero, and_1_out, control_1_alusrc, control_1_branch, control_1_memread, control_1_memreg,
       control_1_memwrite, control_1_regdst, control_1_regwrite;
  wire [1:0] control_1_whb;
  wire [2:0] control_1_aluop;
  wire [4:0] multiplexer_1_out;
  wire [5:0] alucontrol_1_alucode, rom_1_data_2;
  wire [23:0] PC_q;
  wire [31:0] adder_1_out, adder_2_out, datamem_1_readdata, multiplexer_2_out, multiplexer_3_out,
       multiplexer_4_out, PC_q_2, registers_1_readdata1, registers_1_readdata2, shift_l_2_1_shiftout,
       signexit_1_sigout;
  wire [31:6] rom_1_data;

  Register #(.width(32)) PC (
    .D(multiplexer_3_out), .en(1'b1), .clk(Clock), .Q({PC_q_2[31:26], PC_q, PC_q_2[1:0]}), .clr(Clear));
  ROM #(.addrWidth(24), .dataWidth(32)) rom_1 (.addr(PC_q), .data({rom_1_data, rom_1_data_2}));
  Adder #(.width(32)) adder_1 (
    .a({PC_q_2[31:26], PC_q, PC_q_2[1:0]}), .b(32'h4), .out(adder_1_out));  // open: cin, cout
  Control control_1 (
    .Op(rom_1_data[31:26]), .RegDst(control_1_regdst), .Branch(control_1_branch),
    .MemRead(control_1_memread), .MemReg(control_1_memreg), .ALUop(control_1_aluop),
    .MemWrite(control_1_memwrite), .ALUSrc(control_1_alusrc), .RegWrite(control_1_regwrite),
    .WHB(control_1_whb));
  // Probe on rom_1_data[25:21]
  // Probe on rom_1_data[20:16]
  // Probe on multiplexer_1_out
  Multiplexer #(.width(5), .enable("false")) multiplexer_1 (
    .in0(rom_1_data[20:16]), .in1(rom_1_data[15:11]), .out(multiplexer_1_out), .sel(control_1_regdst));
  SignExit signexit_1 (.SigIn({rom_1_data[15:6], rom_1_data_2}), .SigOut(signexit_1_sigout));
  Registers registers_1 (
    .ReadRegister1(rom_1_data[25:21]), .ReadRegister2(rom_1_data[20:16]), .WriteData(multiplexer_4_out),
    .Write(control_1_regwrite), .Clock(Clock), .WriteRegister(multiplexer_1_out),
    .ReadData1(registers_1_readdata1), .ReadData2(registers_1_readdata2));
  Multiplexer #(.width(32), .enable("false")) multiplexer_2 (
    .in0(registers_1_readdata2), .in1(signexit_1_sigout), .out(multiplexer_2_out), .sel(control_1_alusrc));
  Shift_L_2 shift_l_2_1 (.ShitfIn(signexit_1_sigout), .ShiftOut(shift_l_2_1_shiftout));
  // Probe on multiplexer_2_out
  // Probe on alucontrol_1_alucode
  ALUcontrol alucontrol_1 (.Instructions(rom_1_data_2), .ALUop(control_1_aluop), .ALUcode(alucontrol_1_alucode));
  Adder #(.width(32)) adder_2 (.a(adder_1_out), .b(shift_l_2_1_shiftout), .out(adder_2_out));  // open: cin, cout
  and and_1 (and_1_out, control_1_branch, alu_1_zero);
  Multiplexer #(.width(32), .enable("false")) multiplexer_3 (
    .in0(adder_1_out), .in1(adder_2_out), .out(multiplexer_3_out), .sel(and_1_out));
  ALU alu_1 (
    .in0(registers_1_readdata1), .in1(multiplexer_2_out), .ALUcontrol(alucontrol_1_alucode),
    .ALUresult(out_3), .zero(alu_1_zero));
  // Probe on control_1_whb
  DataMem datamem_1 (
    .Adress(out_3), .WriteData(registers_1_readdata2), .WHB(control_1_whb), .MenWrite(control_1_memwrite),
    .OutputEnable(control_1_memread), .Clock(Clock), .ReadData(datamem_1_readdata));
  Multiplexer #(.width(32), .enable("false")) multiplexer_4 (
    .in0(out_3), .in1(datamem_1_readdata), .out(multiplexer_4_out), .sel(control_1_memreg));

  // Notes on the sheet:
  //   contents of rom_1 (hex, n*v repeats v):
  //   221820 221822 221824 221825 221827 221821 221823 20230001 24230001 3023ffff 34230000 8c230000
  //   94230000 90230000 ac230000 a4230000 a0230000 3c010001 1422fff8 1021fff8
  //   add
  //   sub
  //   and
  //   or
  //   nor
  //   addu
  //   subu
  //   addi
  //   addui
  //   andi
  //   ori
  //   lw
  //   lhu
  //   lbu
  //   Sw
  //   sh
  //   sb
endmodule

module SignExit (
  input  [15:0] SigIn,
  output [31:0] SigOut
);


  assign SigOut = {{17{SigIn[15]}}, SigIn[14:0]};
endmodule

module Shift_L_2 (
  input  [31:0] ShitfIn,
  output [31:0] ShiftOut
);


  assign ShiftOut = {ShitfIn[29:0], 2'b00};
endmodule

module DataMem (
  input  [31:0] Adress,
  input  [31:0] WriteData,
  input  [1:0] WHB,
  input  MenWrite,
  input  OutputEnable,
  input  Clock,
  output [31:0] ReadData
);

  wire [1:0] demultiplexer_1_out0, demultiplexer_1_out1;
  wire [3:0] demultiplexer_2_out0, multiplexer_1_out;
  wire [7:0] demultiplexer_3_out0, demultiplexer_3_out1, demultiplexer_3_out2, demultiplexer_3_out3,
       multiplexer_4_out, ram_1_dout, ram_2_dout, ram_3_dout, ram_4_dout;
  wire [15:0] demultiplexer_4_out0, demultiplexer_4_out1, multiplexer_3_out;
  wire [31:0] multiplexer_2_out;

  Demultiplexer #(.width(2), .enable("false")) demultiplexer_1 (
    .out0(demultiplexer_1_out0), .out1(demultiplexer_1_out1), .in({2{MenWrite}}), .sel(Adress[1]));
  Demultiplexer #(.select(2), .enable("false")) demultiplexer_2 (
    .out0(demultiplexer_2_out0[0]), .out1(demultiplexer_2_out0[1]), .out2(demultiplexer_2_out0[2]),
    .out3(demultiplexer_2_out0[3]), .in(MenWrite), .sel(Adress[1:0]));
  Demultiplexer #(.select(2), .width(8), .enable("false")) demultiplexer_3 (
    .out0(demultiplexer_3_out0), .out1(demultiplexer_3_out1), .out2(demultiplexer_3_out2),
    .out3(demultiplexer_3_out3), .in(WriteData[7:0]), .sel(Adress[1:0]));
  Demultiplexer #(.width(16), .enable("false")) demultiplexer_4 (
    .out0(demultiplexer_4_out0), .out1(demultiplexer_4_out1), .in(WriteData[15:0]), .sel(Adress[1]));
  Multiplexer #(.select(2), .width(4), .enable("false")) multiplexer_1 (
    .in0({4{MenWrite}}), .in1({demultiplexer_1_out1, demultiplexer_1_out0}), .in2(demultiplexer_2_out0),
    .in3(4'b0000), .out(multiplexer_1_out), .sel(WHB));
  Multiplexer #(.select(2), .width(32), .enable("false")) multiplexer_2 (
    .in0(WriteData), .in1({demultiplexer_4_out1, demultiplexer_4_out0}),
    .in2({demultiplexer_3_out3, demultiplexer_3_out2, demultiplexer_3_out1, demultiplexer_3_out0}),
    .in3({32{1'b0}}), .out(multiplexer_2_out), .sel(WHB));
  // Probe on multiplexer_2_out[31:24]
  RAM #(.addrWidth(24), .trigger("falling"), .databus("bibus")) ram_1 (
    .addr(Adress[25:2]), .we(multiplexer_1_out[0]), .oe(OutputEnable), .clk(Clock),
    .din(multiplexer_2_out[7:0]), .dout(ram_1_dout));
  // Probe on multiplexer_2_out[7:0]
  RAM #(.addrWidth(24), .trigger("falling"), .databus("bibus")) ram_2 (
    .addr(Adress[25:2]), .we(multiplexer_1_out[1]), .oe(OutputEnable), .clk(Clock),
    .din(multiplexer_2_out[15:8]), .dout(ram_2_dout));
  // Probe on multiplexer_2_out[15:8]
  RAM #(.addrWidth(24), .trigger("falling"), .databus("bibus")) ram_3 (
    .addr(Adress[25:2]), .we(multiplexer_1_out[2]), .oe(OutputEnable), .clk(Clock),
    .din(multiplexer_2_out[23:16]), .dout(ram_3_dout));
  // Probe on multiplexer_2_out[23:16]
  RAM #(.addrWidth(24), .trigger("falling"), .databus("bibus")) ram_4 (
    .addr(Adress[25:2]), .we(multiplexer_1_out[3]), .oe(OutputEnable), .clk(Clock),
    .din(multiplexer_2_out[31:24]), .dout(ram_4_dout));
  Multiplexer #(.width(16), .enable("false")) multiplexer_3 (
    .in0({ram_2_dout, ram_1_dout}), .in1({ram_4_dout, ram_3_dout}), .out(multiplexer_3_out), .sel(Adress[1]));
  Multiplexer #(.select(2), .width(8), .enable("false")) multiplexer_4 (
    .in0(ram_1_dout), .in1(ram_2_dout), .in2(ram_3_dout), .in3(ram_4_dout), .out(multiplexer_4_out),
    .sel(Adress[1:0]));
  Multiplexer #(.select(2), .width(32), .enable("false")) multiplexer_5 (
    .in0({ram_4_dout, ram_3_dout, ram_2_dout, ram_1_dout}), .in1({{16{1'b0}}, multiplexer_3_out}),
    .in2({{24{1'b0}}, multiplexer_4_out}), .in3({32{1'b0}}), .out(ReadData), .sel(WHB));
endmodule

module ALU (
  input  [31:0] in0,
  input  [31:0] in1,
  input  [5:0] ALUcontrol,
  output [31:0] ALUresult,
  output zero
);

  wire or_2_out;
  wire [31:0] adder_1_out, and_1_out, lui_1_outlui, nor_1_out, or_1_out, subtractor_1_out;
  wire [31:31] comparator_1_eq;

  Adder #(.width(32)) adder_1 (.a(in0), .b(in1), .out(adder_1_out), .cin(1'b0));  // open: cout
  Subtractor #(.width(32)) subtractor_1 (.a(in0), .b(in1), .out(subtractor_1_out), .bin(1'b0));  // open: bout
  assign and_1_out = in0 & in1;  // AND_Gate and_1, 32 bits wide
  assign or_1_out = in0 | in1;  // OR_Gate or_1, 32 bits wide
  Comparator #(.width(32)) comparator_1 (.a(in0), .b(in1), .eq(comparator_1_eq[31]));  // open: gt, lt
  assign nor_1_out = ~(in0 | in1);  // NOR_Gate nor_1, 32 bits wide
  LUI lui_1 (.inLUI(in1), .outLUI(lui_1_outlui));
  // Probe on ALUcontrol[3:0]
  Multiplexer #(.select(4), .width(32), .enable("false")) multiplexer_1 (
    .in0(adder_1_out), .in1(adder_1_out), .in2(subtractor_1_out), .in3(subtractor_1_out), .in4(and_1_out),
    .in5(or_1_out), .in6(lui_1_outlui), .in7(nor_1_out), .in8({32{comparator_1_eq[31]}}), .out(ALUresult),
    .sel(ALUcontrol[3:0]));  // open: in9, in10, in11, in12, in13, in14, in15
  or or_2 (or_2_out, ALUresult[0], ALUresult[1], ALUresult[2], ALUresult[3], ALUresult[4], ALUresult[5], ALUresult[6], ALUresult[7], ALUresult[8], ALUresult[9], ALUresult[10], ALUresult[11], ALUresult[12], ALUresult[13], ALUresult[14], ALUresult[15], ALUresult[17], ALUresult[18], ALUresult[19], ALUresult[20], ALUresult[21], ALUresult[22], ALUresult[23], ALUresult[24], ALUresult[25], ALUresult[26], ALUresult[27], ALUresult[28], ALUresult[29], ALUresult[30], ALUresult[31], ALUresult[16]);
  not not_1 (zero, or_2_out);
endmodule

module Registers (
  input  [4:0] ReadRegister1,
  input  [4:0] ReadRegister2,
  input  [31:0] WriteData,
  input  Write,
  input  Clock,
  input  [4:0] WriteRegister,
  output [31:0] ReadData1,
  output [31:0] ReadData2
);

  wire demultiplexer_1_out0, demultiplexer_1_out1, demultiplexer_1_out2, demultiplexer_1_out3,
       demultiplexer_1_out4, demultiplexer_1_out5, demultiplexer_1_out6, demultiplexer_1_out7,
       demultiplexer_1_out8, demultiplexer_1_out9, demultiplexer_1_out10, demultiplexer_1_out11,
       demultiplexer_1_out12, demultiplexer_1_out13, demultiplexer_1_out14, demultiplexer_1_out15,
       demultiplexer_1_out16, demultiplexer_1_out17, demultiplexer_1_out18, demultiplexer_1_out19,
       demultiplexer_1_out20, demultiplexer_1_out21, demultiplexer_1_out22, demultiplexer_1_out23,
       demultiplexer_1_out24, demultiplexer_1_out25, demultiplexer_1_out26, demultiplexer_1_out27,
       demultiplexer_1_out28, demultiplexer_1_out29, demultiplexer_1_out30, demultiplexer_1_out31;
  wire [31:0] register_1_q, register_2_q, register_3_q, register_4_q, register_5_q, register_6_q,
       register_7_q, register_8_q, register_9_q, register_10_q, register_11_q, register_12_q, register_13_q,
       register_14_q, register_15_q, register_16_q, register_17_q, register_18_q, register_19_q,
       register_20_q, register_21_q, register_22_q, register_23_q, register_24_q, register_25_q,
       register_26_q, register_27_q, register_28_q, register_29_q, register_30_q, register_31_q,
       register_32_q;

  Demultiplexer #(.select(5), .enable("false")) demultiplexer_1 (
    .out0(demultiplexer_1_out0), .out1(demultiplexer_1_out1), .out2(demultiplexer_1_out2),
    .out3(demultiplexer_1_out3), .out4(demultiplexer_1_out4), .out5(demultiplexer_1_out5),
    .out6(demultiplexer_1_out6), .out7(demultiplexer_1_out7), .out8(demultiplexer_1_out8),
    .out9(demultiplexer_1_out9), .out10(demultiplexer_1_out10), .out11(demultiplexer_1_out11),
    .out12(demultiplexer_1_out12), .out13(demultiplexer_1_out13), .out14(demultiplexer_1_out14),
    .out15(demultiplexer_1_out15), .out16(demultiplexer_1_out16), .out17(demultiplexer_1_out17),
    .out18(demultiplexer_1_out18), .out19(demultiplexer_1_out19), .out20(demultiplexer_1_out20),
    .out21(demultiplexer_1_out21), .out22(demultiplexer_1_out22), .out23(demultiplexer_1_out23),
    .out24(demultiplexer_1_out24), .out25(demultiplexer_1_out25), .out26(demultiplexer_1_out26),
    .out27(demultiplexer_1_out27), .out28(demultiplexer_1_out28), .out29(demultiplexer_1_out29),
    .out30(demultiplexer_1_out30), .out31(demultiplexer_1_out31), .in(Write), .sel(WriteRegister));
  Register #(.width(32)) register_1 (
    .D(WriteData), .en(demultiplexer_1_out0), .clk(Clock), .Q(register_1_q), .clr(1'b1));
  Register #(.width(32)) register_2 (
    .D(WriteData), .en(demultiplexer_1_out1), .clk(Clock), .Q(register_2_q), .clr(1'b0));
  Register #(.width(32)) register_3 (
    .D(WriteData), .en(demultiplexer_1_out2), .clk(Clock), .Q(register_3_q), .clr(1'b0));
  Register #(.width(32)) register_4 (
    .D(WriteData), .en(demultiplexer_1_out3), .clk(Clock), .Q(register_4_q), .clr(1'b0));
  Register #(.width(32)) register_5 (
    .D(WriteData), .en(demultiplexer_1_out4), .clk(Clock), .Q(register_5_q), .clr(1'b0));
  Register #(.width(32)) register_6 (
    .D(WriteData), .en(demultiplexer_1_out5), .clk(Clock), .Q(register_6_q), .clr(1'b0));
  Register #(.width(32)) register_7 (
    .D(WriteData), .en(demultiplexer_1_out6), .clk(Clock), .Q(register_7_q), .clr(1'b0));
  Register #(.width(32)) register_8 (
    .D(WriteData), .en(demultiplexer_1_out7), .clk(Clock), .Q(register_8_q), .clr(1'b0));
  Register #(.width(32)) register_9 (
    .D(WriteData), .en(demultiplexer_1_out8), .clk(Clock), .Q(register_9_q), .clr(1'b0));
  Register #(.width(32)) register_10 (
    .D(WriteData), .en(demultiplexer_1_out9), .clk(Clock), .Q(register_10_q), .clr(1'b0));
  Register #(.width(32)) register_11 (
    .D(WriteData), .en(demultiplexer_1_out10), .clk(Clock), .Q(register_11_q), .clr(1'b0));
  Register #(.width(32)) register_12 (
    .D(WriteData), .en(demultiplexer_1_out11), .clk(Clock), .Q(register_12_q), .clr(1'b0));
  Register #(.width(32)) register_13 (
    .D(WriteData), .en(demultiplexer_1_out12), .clk(Clock), .Q(register_13_q), .clr(1'b0));
  Register #(.width(32)) register_14 (
    .D(WriteData), .en(demultiplexer_1_out13), .clk(Clock), .Q(register_14_q), .clr(1'b0));
  Register #(.width(32)) register_15 (
    .D(WriteData), .en(demultiplexer_1_out14), .clk(Clock), .Q(register_15_q), .clr(1'b0));
  Register #(.width(32)) register_16 (
    .D(WriteData), .en(demultiplexer_1_out15), .clk(Clock), .Q(register_16_q), .clr(1'b0));
  Register #(.width(32)) register_17 (
    .D(WriteData), .en(demultiplexer_1_out16), .clk(Clock), .Q(register_17_q), .clr(1'b0));
  Register #(.width(32)) register_18 (
    .D(WriteData), .en(demultiplexer_1_out17), .clk(Clock), .Q(register_18_q), .clr(1'b0));
  Register #(.width(32)) register_19 (
    .D(WriteData), .en(demultiplexer_1_out18), .clk(Clock), .Q(register_19_q), .clr(1'b0));
  Register #(.width(32)) register_20 (
    .D(WriteData), .en(demultiplexer_1_out19), .clk(Clock), .Q(register_20_q), .clr(1'b0));
  Register #(.width(32)) register_21 (
    .D(WriteData), .en(demultiplexer_1_out20), .clk(Clock), .Q(register_21_q), .clr(1'b0));
  Register #(.width(32)) register_22 (
    .D(WriteData), .en(demultiplexer_1_out21), .clk(Clock), .Q(register_22_q), .clr(1'b0));
  Register #(.width(32)) register_23 (
    .D(WriteData), .en(demultiplexer_1_out22), .clk(Clock), .Q(register_23_q), .clr(1'b0));
  Register #(.width(32)) register_24 (
    .D(WriteData), .en(demultiplexer_1_out23), .clk(Clock), .Q(register_24_q), .clr(1'b0));
  Register #(.width(32)) register_25 (
    .D(WriteData), .en(demultiplexer_1_out24), .clk(Clock), .Q(register_25_q), .clr(1'b0));
  Register #(.width(32)) register_26 (
    .D(WriteData), .en(demultiplexer_1_out25), .clk(Clock), .Q(register_26_q), .clr(1'b0));
  Register #(.width(32)) register_27 (
    .D(WriteData), .en(demultiplexer_1_out26), .clk(Clock), .Q(register_27_q), .clr(1'b0));
  Register #(.width(32)) register_28 (
    .D(WriteData), .en(demultiplexer_1_out27), .clk(Clock), .Q(register_28_q), .clr(1'b0));
  Register #(.width(32)) register_29 (
    .D(WriteData), .en(demultiplexer_1_out28), .clk(Clock), .Q(register_29_q), .clr(1'b0));
  Register #(.width(32)) register_30 (
    .D(WriteData), .en(demultiplexer_1_out29), .clk(Clock), .Q(register_30_q), .clr(1'b0));
  Register #(.width(32)) register_31 (
    .D(WriteData), .en(demultiplexer_1_out30), .clk(Clock), .Q(register_31_q), .clr(1'b0));
  Register #(.width(32)) register_32 (
    .D(WriteData), .en(demultiplexer_1_out31), .clk(Clock), .Q(register_32_q), .clr(1'b0));
  Multiplexer #(.select(5), .width(32), .enable("false")) multiplexer_1 (
    .in0(register_1_q), .in1(register_2_q), .in2(register_3_q), .in3(register_4_q), .in4(register_5_q),
    .in5(register_6_q), .in6(register_7_q), .in7(register_8_q), .in8(register_9_q), .in9(register_10_q),
    .in10(register_11_q), .in11(register_12_q), .in12(register_13_q), .in13(register_14_q),
    .in14(register_15_q), .in15(register_16_q), .in16(register_17_q), .in17(register_18_q),
    .in18(register_19_q), .in19(register_20_q), .in20(register_21_q), .in21(register_22_q),
    .in22(register_23_q), .in23(register_24_q), .in24(register_25_q), .in25(register_26_q),
    .in26(register_27_q), .in27(register_28_q), .in28(register_29_q), .in29(register_30_q),
    .in30(register_31_q), .in31(register_32_q), .out(ReadData1), .sel(ReadRegister1));
  Multiplexer #(.select(5), .width(32), .enable("false")) multiplexer_2 (
    .in0(register_1_q), .in1(register_2_q), .in2(register_3_q), .in3(register_4_q), .in4(register_5_q),
    .in5(register_6_q), .in6(register_7_q), .in7(register_8_q), .in8(register_9_q), .in9(register_10_q),
    .in10(register_11_q), .in11(register_12_q), .in12(register_13_q), .in13(register_14_q),
    .in14(register_15_q), .in15(register_16_q), .in16(register_17_q), .in17(register_18_q),
    .in18(register_19_q), .in19(register_20_q), .in20(register_21_q), .in21(register_22_q),
    .in22(register_23_q), .in23(register_24_q), .in24(register_25_q), .in25(register_26_q),
    .in26(register_27_q), .in27(register_28_q), .in28(register_29_q), .in29(register_30_q),
    .in30(register_31_q), .in31(register_32_q), .out(ReadData2), .sel(ReadRegister2));
endmodule

module Control (
  input  [5:0] Op,
  output RegDst,
  output Branch,
  output MemRead,
  output MemReg,
  output [2:0] ALUop,
  output MemWrite,
  output ALUSrc,
  output RegWrite,
  output [1:0] WHB
);

  wire [15:12] rom_1_data;

  ROM #(.addrWidth(6), .dataWidth(16)) rom_1 (
    .addr(Op), .data({rom_1_data, WHB, RegWrite, ALUSrc, MemWrite, ALUop, MemReg, MemRead, Branch, RegDst}));

  // Notes on the sheet:
  //   contents of rom_1 (hex, n*v repeats v):
  //   201 0 0 0 62 52 0 0 310 310 0 0 320 330 0 340 19*0 31c b1c 71c 0 0 990 590 0 190
endmodule

module ALUcontrol (
  input  [5:0] Instructions,
  input  [2:0] ALUop,
  output [5:0] ALUcode
);

  Multiplexer #(.select(3), .width(6), .enable("false")) multiplexer_1 (
    .in0(Instructions), .in1({6{1'b0}}), .in2(6'b000100), .in3(6'b000101), .in4(6'b000110), .in5(6'b001000),
    .in6(6'b000010), .out(ALUcode), .sel(ALUop));  // open: in7
endmodule

module LUI (
  input  [31:0] inLUI,
  output [31:0] outLUI
);


  assign outLUI = {inLUI[15:0], {16{1'b0}}};
endmodule
