// Logisim project mycircbak.circ as structural Verilog: 7 circuits, main circuit intruction_fetcher
module intruction_fetcher (
  input  [31:0] next_PC,
  input  write,
  input  clk,
  output [31:0] PC_4,
  output [31:0] instruction
);

  wire [31:0] PC_q;

  Register #(.width(32)) PC (.D(next_PC), .en(write), .clk(clk), .Q(PC_q), .clr(PC_q[26]));
  ROM #(.addrWidth(24), .dataWidth(32)) InstructionMemory (.addr(PC_q[25:2]), .data(instruction));
  Adder #(.width(32)) adder_1 (.a(PC_q), .b(32'h4), .out(PC_4), .cin(1'b0));  // open: cout

  // Notes on the sheet:
  //   contents of InstructionMemory (hex, n*v repeats v):
  //   16777208*0 11110000 11010000 10101100 110000
endmodule

module registers (
  input  [4:0] r_reg_1,
  input  [4:0] r_reg_0,
  input  wr_enable,
  input  [4:0] wr_addr,
  input  [31:0] data,
  input  ck,
  output [31:0] reg_out_0,
  output [31:0] reg_out_1
);

  wire demultiplexer_1_out0, demultiplexer_1_out1, demultiplexer_1_out2, demultiplexer_1_out3,
       demultiplexer_1_out4, demultiplexer_1_out5, demultiplexer_1_out6, demultiplexer_1_out7,
       demultiplexer_1_out8, demultiplexer_1_out9, demultiplexer_1_out10, demultiplexer_1_out11,
       demultiplexer_1_out12, demultiplexer_1_out13, demultiplexer_1_out14, demultiplexer_1_out15,
       demultiplexer_1_out16, demultiplexer_1_out17, demultiplexer_1_out18, demultiplexer_1_out19,
       demultiplexer_1_out20, demultiplexer_1_out21, demultiplexer_1_out22, demultiplexer_1_out23,
       demultiplexer_1_out24, demultiplexer_1_out25, demultiplexer_1_out26, demultiplexer_1_out27,
       demultiplexer_1_out28, demultiplexer_1_out29, demultiplexer_1_out30, demultiplexer_1_out31;
  wire [31:0] register_1_q, register_2_q, register_3_q, register_4_q, register_5_q, register_6_q,
       register_7_q, register_8_q, register_9_q, register_10_q, register_11_q, register_12_q, register_13_q,
       register_14_q, register_15_q, register_16_q, register_17_q, register_18_q, register_19_q,
       register_20_q, register_21_q, register_22_q, register_23_q, register_24_q, register_25_q,
       register_26_q, register_27_q, register_28_q, register_29_q, register_30_q, register_31_q,
       register_32_q, undriven;

  Demultiplexer #(.select(5), .enable("false")) demultiplexer_1 (
    .out0(demultiplexer_1_out0), .out1(demultiplexer_1_out1), .out2(demultiplexer_1_out2),
    .out3(demultiplexer_1_out3), .out4(demultiplexer_1_out4), .out5(demultiplexer_1_out5),
    .out6(demultiplexer_1_out6), .out7(demultiplexer_1_out7), .out8(demultiplexer_1_out8),
    .out9(demultiplexer_1_out9), .out10(demultiplexer_1_out10), .out11(demultiplexer_1_out11),
    .out12(demultiplexer_1_out12), .out13(demultiplexer_1_out13), .out14(demultiplexer_1_out14),
    .out15(demultiplexer_1_out15), .out16(demultiplexer_1_out16), .out17(demultiplexer_1_out17),
    .out18(demultiplexer_1_out18), .out19(demultiplexer_1_out19), .out20(demultiplexer_1_out20),
    .out21(demultiplexer_1_out21), .out22(demultiplexer_1_out22), .out23(demultiplexer_1_out23),
    .out24(demultiplexer_1_out24), .out25(demultiplexer_1_out25), .out26(demultiplexer_1_out26),
    .out27(demultiplexer_1_out27), .out28(demultiplexer_1_out28), .out29(demultiplexer_1_out29),
    .out30(demultiplexer_1_out30), .out31(demultiplexer_1_out31), .in(wr_enable), .sel(wr_addr));
  Register #(.width(32)) register_1 (.D(data), .en(demultiplexer_1_out0), .clk(ck), .Q(register_1_q), .clr(1'b1));
  Register #(.width(32)) register_2 (.D(data), .en(demultiplexer_1_out1), .clk(ck), .Q(register_2_q), .clr(1'b0));
  Register #(.width(32)) register_3 (.D(data), .en(demultiplexer_1_out2), .clk(ck), .Q(register_3_q), .clr(1'b0));
  Register #(.width(32)) register_4 (.D(data), .en(demultiplexer_1_out3), .clk(ck), .Q(register_4_q), .clr(1'b0));
  Register #(.width(32)) register_5 (.D(data), .en(demultiplexer_1_out4), .clk(ck), .Q(register_5_q), .clr(1'b0));
  Register #(.width(32)) register_6 (.D(data), .en(demultiplexer_1_out5), .clk(ck), .Q(register_6_q), .clr(1'b0));
  Register #(.width(32)) register_7 (.D(data), .en(demultiplexer_1_out6), .clk(ck), .Q(register_7_q), .clr(1'b0));
  Register #(.width(32)) register_8 (.D(data), .en(demultiplexer_1_out7), .clk(ck), .Q(register_8_q), .clr(1'b0));
  Register #(.width(32)) register_9 (.D(data), .en(demultiplexer_1_out8), .clk(ck), .Q(register_9_q), .clr(1'b0));
  Register #(.width(32)) register_10 (.D(data), .en(demultiplexer_1_out9), .clk(ck), .Q(register_10_q), .clr(1'b0));
  Register #(.width(32)) register_11 (.D(data), .en(demultiplexer_1_out10), .clk(ck), .Q(register_11_q), .clr(1'b0));
  Register #(.width(32)) register_12 (.D(data), .en(demultiplexer_1_out11), .clk(ck), .Q(register_12_q), .clr(1'b0));
  Register #(.width(32)) register_13 (.D(data), .en(demultiplexer_1_out12), .clk(ck), .Q(register_13_q), .clr(1'b0));
  Register #(.width(32)) register_14 (.D(data), .en(demultiplexer_1_out13), .clk(ck), .Q(register_14_q), .clr(1'b0));
  Register #(.width(32)) register_15 (.D(data), .en(demultiplexer_1_out14), .clk(ck), .Q(register_15_q), .clr(1'b0));
  Register #(.width(32)) register_16 (.D(data), .en(demultiplexer_1_out15), .clk(ck), .Q(register_16_q), .clr(1'b0));
  Register #(.width(32)) register_17 (.D(data), .en(demultiplexer_1_out16), .clk(ck), .Q(register_17_q), .clr(1'b0));
  Register #(.width(32)) register_18 (.D(data), .en(demultiplexer_1_out17), .clk(ck), .Q(register_18_q), .clr(1'b0));
  Register #(.width(32)) register_19 (.D(data), .en(demultiplexer_1_out18), .clk(ck), .Q(register_19_q), .clr(1'b0));
  Register #(.width(32)) register_20 (.D(data), .en(demultiplexer_1_out19), .clk(ck), .Q(register_20_q), .clr(1'b0));
  Register #(.width(32)) register_21 (.D(data), .en(demultiplexer_1_out20), .clk(ck), .Q(register_21_q), .clr(1'b0));
  Register #(.width(32)) register_22 (.D(data), .en(demultiplexer_1_out21), .clk(ck), .Q(register_22_q), .clr(1'b0));
  Register #(.width(32)) register_23 (.D(data), .en(demultiplexer_1_out22), .clk(ck), .Q(register_23_q), .clr(1'b0));
  Register #(.width(32)) register_24 (.D(data), .en(demultiplexer_1_out23), .clk(ck), .Q(register_24_q), .clr(1'b0));
  Register #(.width(32)) register_25 (
    .D(undriven), .en(demultiplexer_1_out24), .clk(ck), .Q(register_25_q), .clr(1'b0));
  Register #(.width(32)) register_26 (
    .D(undriven), .en(demultiplexer_1_out25), .clk(ck), .Q(register_26_q), .clr(1'b0));
  Register #(.width(32)) register_27 (
    .D(undriven), .en(demultiplexer_1_out26), .clk(ck), .Q(register_27_q), .clr(1'b0));
  Register #(.width(32)) register_28 (
    .D(undriven), .en(demultiplexer_1_out27), .clk(ck), .Q(register_28_q), .clr(1'b0));
  Register #(.width(32)) register_29 (
    .D(undriven), .en(demultiplexer_1_out28), .clk(ck), .Q(register_29_q), .clr(1'b0));
  Register #(.width(32)) register_30 (
    .D(undriven), .en(demultiplexer_1_out29), .clk(ck), .Q(register_30_q), .clr(1'b0));
  Register #(.width(32)) register_31 (
    .D(undriven), .en(demultiplexer_1_out30), .clk(ck), .Q(register_31_q), .clr(1'b0));
  Register #(.width(32)) register_32 (
    .D(undriven), .en(demultiplexer_1_out31), .clk(ck), .Q(register_32_q), .clr(1'b0));
  Multiplexer #(.select(5), .width(32), .enable("false")) multiplexer_1 (
    .in0(register_1_q), .in1(register_2_q), .in2(register_3_q), .in3(register_4_q), .in4(register_5_q),
    .in5(register_6_q), .in6(register_7_q), .in7(register_8_q), .in8(register_9_q), .in9(register_10_q),
    .in10(register_11_q), .in11(register_12_q), .in12(register_13_q), .in13(register_14_q),
    .in14(register_15_q), .in15(register_16_q), .in16(register_17_q), .in17(register_18_q),
    .in18(register_19_q), .in19(register_20_q), .in20(register_21_q), .in21(register_22_q),
    .in22(register_23_q), .in23(register_24_q), .in24(register_25_q), .in25(register_26_q),
    .in26(register_27_q), .in27(register_28_q), .in28(register_29_q), .in29(register_30_q),
    .in30(register_31_q), .in31(register_32_q), .out(reg_out_0), .sel(r_reg_0));
  Multiplexer #(.select(5), .width(32), .enable("false")) multiplexer_2 (
    .in0(register_1_q), .in1(register_2_q), .in2(register_3_q), .in3(register_4_q), .in4(register_5_q),
    .in5(register_6_q), .in6(register_7_q), .in7(register_8_q), .in8(register_9_q), .in9(register_10_q),
    .in10(register_11_q), .in11(register_12_q), .in12(register_13_q), .in13(register_14_q),
    .in14(register_15_q), .in15(register_16_q), .in16(register_17_q), .in17(register_18_q),
    .in18(register_19_q), .in19(register_20_q), .in20(register_21_q), .in21(register_22_q),
    .in22(register_23_q), .in23(register_24_q), .in24(register_25_q), .in25(register_26_q),
    .in26(register_27_q), .in27(register_28_q), .in28(register_29_q), .in29(register_30_q),
    .in30(register_31_q), .in31(register_32_q), .out(reg_out_1), .sel(r_reg_1));
endmodule

module ALU (
  input  [31:0] ALU_in0,
  input  [31:0] ALU_in1,
  input  [2:0] ALU_op,
  output [31:0] ALU_out,
  output is_0
);

  wire [31:0] adder_1_out, and_1_out, nor_1_out, or_1_out, subtractor_1_out;

  Adder #(.width(32)) adder_1 (.a(ALU_in0), .b(ALU_in1), .out(adder_1_out), .cin(1'b0));  // open: cout
  Subtractor #(.width(32)) subtractor_1 (.a(ALU_in0), .b(ALU_in1), .out(subtractor_1_out), .bin(1'b0));  // open: bout
  assign and_1_out = ALU_in0 & ALU_in1;  // AND_Gate and_1, 32 bits wide
  assign or_1_out = ALU_in0 | ALU_in1;  // OR_Gate or_1, 32 bits wide
  assign nor_1_out = ~(ALU_in0 | ALU_in1);  // NOR_Gate nor_1, 32 bits wide
  Multiplexer #(.select(3), .width(32), .enable("false")) multiplexer_1 (
    .in0(adder_1_out), .in1(subtractor_1_out), .in2(and_1_out), .in3(or_1_out), .in4(nor_1_out),
    .out(ALU_out), .sel(ALU_op));  // open: in5, in6, in7
  nor nor_2 (is_0, ALU_out[0], ALU_out[1], ALU_out[2], ALU_out[3], ALU_out[4], ALU_out[5], ALU_out[6], ALU_out[7], ALU_out[8], ALU_out[9], ALU_out[10], ALU_out[11], ALU_out[12], ALU_out[13], ALU_out[14], ALU_out[15], ALU_out[17], ALU_out[18], ALU_out[19], ALU_out[20], ALU_out[21], ALU_out[22], ALU_out[23], ALU_out[24], ALU_out[25], ALU_out[26], ALU_out[27], ALU_out[28], ALU_out[29], ALU_out[30], ALU_out[31], ALU_out[16]);
endmodule

module main (
  input  clk,
  input  in_2,
  input  in_3,
  input  write,
  input  in_5,
  input  in_6,
  input  [1:0] in_7,
  input  in_8,
  input  [2:0] alu_op,
  input  in_10,
  input  in_11,
  output is_0
);

  wire [4:0] multiplexer_1_out;
  wire [31:0] adder_1_out, alu_1_alu_out, data_memory_1_out_7, intruction_fetcher_1_instruction,
       intruction_fetcher_1_pc_4, multiplexer_2_out, multiplexer_3_out, multiplexer_4_out,
       registers_1_reg_out_0, registers_1_reg_out_1, shift_2_1_shift_out, signal_extender_1_sigextout;

  // Probe on multiplexer_3_out
  // Probe on intruction_fetcher_1_instruction
  intruction_fetcher intruction_fetcher_1 (
    .next_PC(multiplexer_3_out), .write(write), .clk(clk), .PC_4(intruction_fetcher_1_pc_4),
    .instruction(intruction_fetcher_1_instruction));
  // Probe on intruction_fetcher_1_instruction[25:21]
  // Probe on intruction_fetcher_1_instruction[20:16]
  Multiplexer #(.width(5), .enable("false")) multiplexer_1 (
    .in0(intruction_fetcher_1_instruction[20:16]), .in1(intruction_fetcher_1_instruction[15:11]),
    .out(multiplexer_1_out), .sel(in_11));
  // Probe on multiplexer_4_out
  // Probe on multiplexer_1_out
  signal_extender signal_extender_1 (
    .sigextin(intruction_fetcher_1_instruction[15:0]), .sigextout(signal_extender_1_sigextout));
  registers registers_1 (
    .reg_out_0(registers_1_reg_out_0), .data(multiplexer_4_out), .wr_enable(in_5),
    .r_reg_1(intruction_fetcher_1_instruction[20:16]), .r_reg_0(intruction_fetcher_1_instruction[25:21]),
    .wr_addr(multiplexer_1_out), .ck(clk), .reg_out_1(registers_1_reg_out_1));
  // Probe on registers_1_reg_out_0
  // Probe on registers_1_reg_out_1
  shift_2 shift_2_1 (.Shift_In(signal_extender_1_sigextout), .Shift_Out(shift_2_1_shift_out));
  Multiplexer #(.width(32), .enable("false")) multiplexer_2 (
    .in0(registers_1_reg_out_1), .in1(signal_extender_1_sigextout), .out(multiplexer_2_out), .sel(in_3));
  Adder #(.width(32)) adder_1 (
    .a(intruction_fetcher_1_pc_4), .b(shift_2_1_shift_out), .out(adder_1_out), .cin(1'b0));  // open: cout
  Multiplexer #(.width(32), .enable("false")) multiplexer_3 (
    .in0(intruction_fetcher_1_pc_4), .in1(adder_1_out), .out(multiplexer_3_out), .sel(in_2));
  ALU alu_1 (
    .ALU_in0(registers_1_reg_out_0), .ALU_in1(multiplexer_2_out), .ALU_op(alu_op), .ALU_out(alu_1_alu_out),
    .is_0(is_0));
  // Probe on alu_1_alu_out
  data_memory data_memory_1 (
    .addr(alu_1_alu_out), .data(registers_1_reg_out_1), .write_en(in_6), .whb(in_7), .read(in_10), .clk(clk),
    .out_7(data_memory_1_out_7));
  Multiplexer #(.width(32), .enable("false")) multiplexer_4 (
    .in0(data_memory_1_out_7), .in1(alu_1_alu_out), .out(multiplexer_4_out), .sel(in_8));
endmodule

module data_memory (
  input  [31:0] addr,
  input  [31:0] data,
  input  write_en,
  input  [1:0] whb,
  input  read,
  input  clk,
  output [31:0] out_7
);

  wire [1:0] demultiplexer_1_out0, demultiplexer_1_out1;
  wire [3:0] demultiplexer_2_out0, multiplexer_2_out;
  wire [7:0] demultiplexer_4_out0, demultiplexer_4_out1, demultiplexer_4_out2, demultiplexer_4_out3,
       multiplexer_4_out, ram_1_dout, ram_2_dout, ram_3_dout, ram_4_dout;
  wire [15:0] demultiplexer_3_out0, demultiplexer_3_out1, multiplexer_3_out;
  wire [31:0] multiplexer_1_out;

  Demultiplexer #(.width(2), .enable("false")) demultiplexer_1 (
    .out0(demultiplexer_1_out0), .out1(demultiplexer_1_out1), .in({2{write_en}}), .sel(addr[1]));
  Demultiplexer #(.select(2), .enable("false")) demultiplexer_2 (
    .out0(demultiplexer_2_out0[0]), .out1(demultiplexer_2_out0[1]), .out2(demultiplexer_2_out0[2]),
    .out3(demultiplexer_2_out0[3]), .in(write_en), .sel({addr[0], addr[1]}));
  Demultiplexer #(.width(16), .enable("false")) demultiplexer_3 (
    .out0(demultiplexer_3_out0), .out1(demultiplexer_3_out1), .in(data[15:0]), .sel(addr[1]));
  Demultiplexer #(.select(2), .width(8), .enable("false")) demultiplexer_4 (
    .out0(demultiplexer_4_out0), .out1(demultiplexer_4_out1), .out2(demultiplexer_4_out2),
    .out3(demultiplexer_4_out3), .in(data[7:0]), .sel({addr[0], addr[1]}));
  Multiplexer #(.select(2), .width(32), .enable("false")) multiplexer_1 (
    .in0(data), .in1({demultiplexer_3_out1, demultiplexer_3_out0}),
    .in2({demultiplexer_4_out3, demultiplexer_4_out2, demultiplexer_4_out1, demultiplexer_4_out0}),
    .out(multiplexer_1_out), .sel(whb));  // open: in3
  Multiplexer #(.select(2), .width(4), .enable("false")) multiplexer_2 (
    .in0({4{write_en}}), .in1({demultiplexer_1_out1, demultiplexer_1_out0}), .in2(demultiplexer_2_out0),
    .out(multiplexer_2_out), .sel(whb));  // open: in3
  // Probe on addr[25:2]
  RAM #(.addrWidth(24), .databus("bibus")) ram_1 (
    .addr(addr[25:2]), .we(multiplexer_2_out[0]), .oe(read), .clk(clk), .din(multiplexer_1_out[7:0]),
    .dout(ram_1_dout));
  RAM #(.addrWidth(24), .databus("bibus")) ram_2 (
    .addr(addr[25:2]), .we(multiplexer_2_out[1]), .oe(read), .clk(clk), .din(multiplexer_1_out[15:8]),
    .dout(ram_2_dout));
  RAM #(.addrWidth(24), .databus("bibus")) ram_3 (
    .addr(addr[25:2]), .we(multiplexer_2_out[2]), .oe(read), .clk(clk), .din(multiplexer_1_out[23:16]),
    .dout(ram_3_dout));
  RAM #(.addrWidth(24), .databus("bibus")) ram_4 (
    .addr(addr[25:2]), .we(multiplexer_2_out[3]), .oe(read), .clk(clk), .din(multiplexer_1_out[31:24]),
    .dout(ram_4_dout));
  // Probe on ram_1_dout
  // Probe on ram_2_dout
  // Probe on ram_3_dout
  // Probe on ram_4_dout
  Multiplexer #(.width(16), .enable("false")) multiplexer_3 (
    .in0({ram_2_dout, ram_1_dout}), .in1({ram_4_dout, ram_3_dout}), .out(multiplexer_3_out), .sel(addr[0]));
  Multiplexer #(.select(2), .width(8), .enable("false")) multiplexer_4 (
    .in0(ram_1_dout), .in1(ram_2_dout), .in2(ram_3_dout), .in3(ram_4_dout), .out(multiplexer_4_out),
    .sel(addr[1:0]));
  Multiplexer #(.select(2), .width(32), .enable("false")) multiplexer_5 (
    .in0({ram_4_dout, ram_3_dout, ram_2_dout, ram_1_dout}), .in1({{24{1'b0}}, multiplexer_4_out}),
    .in2({{16{1'b0}}, multiplexer_3_out}), .out(out_7), .sel(whb));  // open: in3
endmodule

module signal_extender (
  input  [15:0] sigextin,
  output [31:0] sigextout
);


  assign sigextout = {{17{sigextin[15]}}, sigextin[14:0]};
endmodule

module shift_2 (
  input  [31:0] Shift_In,
  output [31:0] Shift_Out
);


  assign Shift_Out = {Shift_In[29:0], 2'b00};
endmodule
