// Logisim project trabalho_3_arq_comp_salgado.circ as structural Verilog: 7 circuits, main circuit main
module main (
  input  in_1,
  input  in_2,
  input  [1:0] in_3,
  input  in_4,
  input  in_5,
  input  in_6,
  input  in_7,
  input  in_8,
  input  in_9,
  input  clk,
  input  [2:0] in_11,
  output out_12
);

  wire [4:0] multiplexer_1_out;
  wire [31:0] adder_1_out, alu_1_alu_out, circuito_de_busca_1_instruction, circuito_de_busca_1_pc_4,
       memorias_1_read_data, multiplexer_2_out, multiplexer_3_out, multiplexer_4_out,
       registers_1_read_data_1, registers_1_read_data_2, shift2_1_shiftout, signalextend_1_signalxout;

  circuito_de_busca circuito_de_busca_1 (
    .Next_PC(multiplexer_3_out), .Write(in_4), .clk(clk), .PC_4(circuito_de_busca_1_pc_4),
    .instruction(circuito_de_busca_1_instruction));
  Multiplexer #(.width(5), .enable("false")) multiplexer_1 (
    .in0(circuito_de_busca_1_instruction[20:16]), .in1(circuito_de_busca_1_instruction[15:11]),
    .out(multiplexer_1_out), .sel(in_9));
  signalExtend signalextend_1 (
    .SignalXIn(circuito_de_busca_1_instruction[15:0]), .signalXOut(signalextend_1_signalxout));
  Registers registers_1 (
    .Data_write(multiplexer_4_out), .Read_Register_1(circuito_de_busca_1_instruction[25:21]), .Write(in_7),
    .Write_Register(multiplexer_1_out), .Read_Data_2(registers_1_read_data_2),
    .Read_Register_2(circuito_de_busca_1_instruction[20:16]), .Read_Data_1(registers_1_read_data_1), .clk(clk));
  Shift2 shift2_1 (.ShiftIn(signalextend_1_signalxout), .ShiftOut(shift2_1_shiftout));
  Multiplexer #(.width(32), .enable("false")) multiplexer_2 (
    .in0(registers_1_read_data_2), .in1(signalextend_1_signalxout), .out(multiplexer_2_out), .sel(in_2));
  Adder #(.width(32)) adder_1 (
    .a(circuito_de_busca_1_pc_4), .b(shift2_1_shiftout), .out(adder_1_out), .cin(1'b0));  // open: cout
  ALU alu_1 (
    .In_1(registers_1_read_data_1), .In_2(multiplexer_2_out), .ALU_Op(in_11), .ALU_out(alu_1_alu_out),
    .Zero(out_12));
  Multiplexer #(.width(32), .enable("false")) multiplexer_3 (
    .in0(circuito_de_busca_1_pc_4), .in1(adder_1_out), .out(multiplexer_3_out), .sel(in_1));
  memorias memorias_1 (
    .Addres(alu_1_alu_out), .Data(registers_1_read_data_2), .whb(in_3), .write(in_5), .read(in_8), .clk(clk),
    .Read_Data(memorias_1_read_data));
  Multiplexer #(.width(32), .enable("false")) multiplexer_4 (
    .in0(memorias_1_read_data), .in1(alu_1_alu_out), .out(multiplexer_4_out), .sel(in_6));
endmodule

module Registers (
  input  [4:0] Read_Register_1,
  input  [4:0] Read_Register_2,
  input  [4:0] Write_Register,
  input  [31:0] Data_write,
  input  Write,
  input  clk,
  output [31:0] Read_Data_1,
  output [31:0] Read_Data_2
);

  wire demultiplexer_1_out0, demultiplexer_1_out1, demultiplexer_1_out2, demultiplexer_1_out3,
       demultiplexer_1_out4, demultiplexer_1_out5, demultiplexer_1_out6, demultiplexer_1_out7,
       demultiplexer_1_out8, demultiplexer_1_out9, demultiplexer_1_out10, demultiplexer_1_out11,
       demultiplexer_1_out12, demultiplexer_1_out13, demultiplexer_1_out14, demultiplexer_1_out15,
       demultiplexer_1_out16, demultiplexer_1_out17, demultiplexer_1_out18, demultiplexer_1_out19,
       demultiplexer_1_out20, demultiplexer_1_out21, demultiplexer_1_out22, demultiplexer_1_out23,
       demultiplexer_1_out24, demultiplexer_1_out25, demultiplexer_1_out26, demultiplexer_1_out27,
       demultiplexer_1_out28, demultiplexer_1_out29, demultiplexer_1_out30, demultiplexer_1_out31;
  wire [31:0] register_1_q, register_2_q, register_3_q, register_4_q, register_5_q, register_6_q,
       register_7_q, register_8_q, register_9_q, register_10_q, register_11_q, register_12_q, register_13_q,
       register_14_q, register_15_q, register_16_q, register_17_q, register_18_q, register_19_q,
       register_20_q, register_21_q, register_22_q, register_23_q, register_24_q, register_25_q,
       register_26_q, register_27_q, register_28_q, register_29_q, register_30_q, register_31_q,
       register_32_q;

  Demultiplexer #(.select(5), .enable("false")) demultiplexer_1 (
    .out0(demultiplexer_1_out0), .out1(demultiplexer_1_out1), .out2(demultiplexer_1_out2),
    .out3(demultiplexer_1_out3), .out4(demultiplexer_1_out4), .out5(demultiplexer_1_out5),
    .out6(demultiplexer_1_out6), .out7(demultiplexer_1_out7), .out8(demultiplexer_1_out8),
    .out9(demultiplexer_1_out9), .out10(demultiplexer_1_out10), .out11(demultiplexer_1_out11),
    .out12(demultiplexer_1_out12), .out13(demultiplexer_1_out13), .out14(demultiplexer_1_out14),
    .out15(demultiplexer_1_out15), .out16(demultiplexer_1_out16), .out17(demultiplexer_1_out17),
    .out18(demultiplexer_1_out18), .out19(demultiplexer_1_out19), .out20(demultiplexer_1_out20),
    .out21(demultiplexer_1_out21), .out22(demultiplexer_1_out22), .out23(demultiplexer_1_out23),
    .out24(demultiplexer_1_out24), .out25(demultiplexer_1_out25), .out26(demultiplexer_1_out26),
    .out27(demultiplexer_1_out27), .out28(demultiplexer_1_out28), .out29(demultiplexer_1_out29),
    .out30(demultiplexer_1_out30), .out31(demultiplexer_1_out31), .in(Write), .sel(Write_Register));
  Register #(.width(32)) register_1 (
    .D(Data_write), .en(demultiplexer_1_out0), .clk(clk), .Q(register_1_q), .clr(1'b1));
  Register #(.width(32)) register_2 (
    .D(Data_write), .en(demultiplexer_1_out1), .clk(clk), .Q(register_2_q), .clr(1'b0));
  Register #(.width(32)) register_3 (
    .D(Data_write), .en(demultiplexer_1_out2), .clk(clk), .Q(register_3_q), .clr(1'b0));
  Register #(.width(32)) register_4 (
    .D(Data_write), .en(demultiplexer_1_out3), .clk(clk), .Q(register_4_q), .clr(1'b0));
  Register #(.width(32)) register_5 (
    .D(Data_write), .en(demultiplexer_1_out4), .clk(clk), .Q(register_5_q), .clr(1'b0));
  Register #(.width(32)) register_6 (
    .D(Data_write), .en(demultiplexer_1_out5), .clk(clk), .Q(register_6_q), .clr(1'b0));
  Register #(.width(32)) register_7 (
    .D(Data_write), .en(demultiplexer_1_out6), .clk(clk), .Q(register_7_q), .clr(1'b0));
  Register #(.width(32)) register_8 (
    .D(Data_write), .en(demultiplexer_1_out7), .clk(clk), .Q(register_8_q), .clr(1'b0));
  Register #(.width(32)) register_9 (
    .D(Data_write), .en(demultiplexer_1_out15), .clk(clk), .Q(register_9_q), .clr(1'b0));
  Register #(.width(32)) register_10 (
    .D(Data_write), .en(demultiplexer_1_out14), .clk(clk), .Q(register_10_q), .clr(1'b0));
  Register #(.width(32)) register_11 (.en(demultiplexer_1_out13), .clk(clk), .Q(register_11_q), .clr(1'b0));  // open: D
  Register #(.width(32)) register_12 (
    .D(Data_write), .en(demultiplexer_1_out12), .clk(clk), .Q(register_12_q), .clr(1'b0));
  Register #(.width(32)) register_13 (
    .D(Data_write), .en(demultiplexer_1_out11), .clk(clk), .Q(register_13_q), .clr(1'b0));
  Register #(.width(32)) register_14 (
    .D(Data_write), .en(demultiplexer_1_out10), .clk(clk), .Q(register_14_q), .clr(1'b0));
  Register #(.width(32)) register_15 (
    .D(Data_write), .en(demultiplexer_1_out9), .clk(clk), .Q(register_15_q), .clr(1'b0));
  Register #(.width(32)) register_16 (
    .D(Data_write), .en(demultiplexer_1_out8), .clk(clk), .Q(register_16_q), .clr(1'b0));
  Register #(.width(32)) register_17 (
    .D(Data_write), .en(demultiplexer_1_out23), .clk(clk), .Q(register_17_q), .clr(1'b0));
  Register #(.width(32)) register_18 (
    .D(Data_write), .en(demultiplexer_1_out22), .clk(clk), .Q(register_18_q), .clr(1'b0));
  Register #(.width(32)) register_19 (
    .D(Data_write), .en(demultiplexer_1_out21), .clk(clk), .Q(register_19_q), .clr(1'b0));
  Register #(.width(32)) register_20 (
    .D(Data_write), .en(demultiplexer_1_out20), .clk(clk), .Q(register_20_q), .clr(1'b0));
  Register #(.width(32)) register_21 (
    .D(Data_write), .en(demultiplexer_1_out19), .clk(clk), .Q(register_21_q), .clr(1'b0));
  Register #(.width(32)) register_22 (
    .D(Data_write), .en(demultiplexer_1_out18), .clk(clk), .Q(register_22_q), .clr(1'b0));
  Register #(.width(32)) register_23 (
    .D(Data_write), .en(demultiplexer_1_out17), .clk(clk), .Q(register_23_q), .clr(1'b0));
  Register #(.width(32)) register_24 (
    .D(Data_write), .en(demultiplexer_1_out16), .clk(clk), .Q(register_24_q), .clr(1'b0));
  Register #(.width(32)) register_25 (
    .D(Data_write), .en(demultiplexer_1_out31), .clk(clk), .Q(register_25_q), .clr(1'b0));
  Register #(.width(32)) register_26 (
    .D(Data_write), .en(demultiplexer_1_out30), .clk(clk), .Q(register_26_q), .clr(1'b0));
  Register #(.width(32)) register_27 (
    .D(Data_write), .en(demultiplexer_1_out29), .clk(clk), .Q(register_27_q), .clr(1'b0));
  Register #(.width(32)) register_28 (
    .D(Data_write), .en(demultiplexer_1_out28), .clk(clk), .Q(register_28_q), .clr(1'b0));
  Register #(.width(32)) register_29 (
    .D(Data_write), .en(demultiplexer_1_out27), .clk(clk), .Q(register_29_q), .clr(1'b0));
  Register #(.width(32)) register_30 (
    .D(Data_write), .en(demultiplexer_1_out26), .clk(clk), .Q(register_30_q), .clr(1'b0));
  Register #(.width(32)) register_31 (
    .D(Data_write), .en(demultiplexer_1_out25), .clk(clk), .Q(register_31_q), .clr(1'b0));
  Register #(.width(32)) register_32 (
    .D(Data_write), .en(demultiplexer_1_out24), .clk(clk), .Q(register_32_q), .clr(1'b0));
  Multiplexer #(.select(5), .width(32), .enable("false")) multiplexer_1 (
    .in0(register_1_q), .in1(register_2_q), .in2(register_3_q), .in3(register_4_q), .in4(register_5_q),
    .in5(register_6_q), .in6(register_7_q), .in7(register_8_q), .in8(register_9_q), .in9(register_10_q),
    .in10(register_11_q), .in11(register_12_q), .in12(register_13_q), .in13(register_14_q),
    .in14(register_15_q), .in15(register_16_q), .in16(register_17_q), .in17(register_18_q),
    .in18(register_19_q), .in19(register_20_q), .in20(register_21_q), .in21(register_22_q),
    .in22(register_23_q), .in23(register_24_q), .in24(register_25_q), .in25(register_26_q),
    .in26(register_27_q), .in27(register_28_q), .in28(register_29_q), .in29(register_30_q),
    .in30(register_31_q), .in31(register_32_q), .out(Read_Data_1), .sel(Read_Register_1));
  Multiplexer #(.select(5), .width(32), .enable("false")) multiplexer_2 (
    .in0(register_1_q), .in1(register_2_q), .in2(register_3_q), .in3(register_4_q), .in4(register_5_q),
    .in5(register_6_q), .in6(register_7_q), .in7(register_8_q), .in8(register_9_q), .in9(register_10_q),
    .in10(register_11_q), .in11(register_12_q), .in12(register_13_q), .in13(register_14_q),
    .in14(register_15_q), .in15(register_16_q), .in16(register_17_q), .in17(register_18_q),
    .in18(register_19_q), .in19(register_20_q), .in20(register_21_q), .in21(register_22_q),
    .in22(register_23_q), .in23(register_24_q), .in24(register_25_q), .in25(register_26_q),
    .in26(register_27_q), .in27(register_28_q), .in28(register_29_q), .in29(register_30_q),
    .in30(register_31_q), .in31(register_32_q), .out(Read_Data_2), .sel(Read_Register_2));
endmodule

module ALU (
  input  [31:0] In_1,
  input  [31:0] In_2,
  input  [2:0] ALU_Op,
  output [31:0] ALU_out,
  output Zero
);

  wire or_2_out;
  wire [31:0] adder_1_out, and_1_out, nor_1_out, or_1_out, subtractor_1_out;

  Adder #(.width(32)) adder_1 (.a(In_1), .b(In_2), .out(adder_1_out), .cin(1'b0));  // open: cout
  Subtractor #(.width(32)) subtractor_1 (.a(In_1), .b(In_2), .out(subtractor_1_out), .bin(1'b0));  // open: bout
  assign and_1_out = In_1 & In_2;  // AND_Gate and_1, 32 bits wide
  assign or_1_out = In_1 | In_2;  // OR_Gate or_1, 32 bits wide
  assign nor_1_out = ~(In_1 | In_2);  // NOR_Gate nor_1, 32 bits wide
  Multiplexer #(.select(3), .width(32), .enable("false")) multiplexer_1 (
    .in0(adder_1_out), .in1(subtractor_1_out), .in2(and_1_out), .in3(or_1_out), .in4(nor_1_out),
    .out(ALU_out), .sel(ALU_Op));  // open: in5, in6, in7
  or or_2 (or_2_out, ALU_out[0], ALU_out[1], ALU_out[2], ALU_out[3], ALU_out[4], ALU_out[5], ALU_out[6], ALU_out[7], ALU_out[8], ALU_out[9], ALU_out[10], ALU_out[11], ALU_out[12], ALU_out[13], ALU_out[14], ALU_out[15], ALU_out[17], ALU_out[18], ALU_out[19], ALU_out[20], ALU_out[21], ALU_out[22], ALU_out[23], ALU_out[24], ALU_out[25], ALU_out[26], ALU_out[27], ALU_out[28], ALU_out[29], ALU_out[30], ALU_out[31], ALU_out[16]);
  not not_1 (Zero, or_2_out);
endmodule

module memorias (
  input  [31:0] Addres,
  input  [31:0] Data,
  input  [1:0] whb,
  input  write,
  input  read,
  input  clk,
  output [31:0] Read_Data
);

  wire [1:0] demultiplexer_4_out0, demultiplexer_4_out1;
  wire [3:0] demultiplexer_1_out0, multiplexer_2_out;
  wire [7:0] demultiplexer_3_out0, demultiplexer_3_out1, demultiplexer_3_out2, demultiplexer_3_out3,
       multiplexer_4_out, ram_1_dout, ram_2_dout, ram_3_dout, ram_4_dout;
  wire [15:0] demultiplexer_2_out0, demultiplexer_2_out1, multiplexer_3_out;
  wire [31:0] multiplexer_1_out;

  Demultiplexer #(.select(2), .enable("false")) demultiplexer_1 (
    .out0(demultiplexer_1_out0[0]), .out1(demultiplexer_1_out0[1]), .out2(demultiplexer_1_out0[2]),
    .out3(demultiplexer_1_out0[3]), .in(write), .sel(Addres[1:0]));
  Demultiplexer #(.width(16), .enable("false")) demultiplexer_2 (
    .out0(demultiplexer_2_out0), .out1(demultiplexer_2_out1), .in(Data[15:0]), .sel(Addres[1]));
  Demultiplexer #(.select(2), .width(8), .enable("false")) demultiplexer_3 (
    .out0(demultiplexer_3_out0), .out1(demultiplexer_3_out1), .out2(demultiplexer_3_out2),
    .out3(demultiplexer_3_out3), .in(Data[7:0]), .sel(Addres[1:0]));
  Demultiplexer #(.width(2), .enable("false")) demultiplexer_4 (
    .out0(demultiplexer_4_out0), .out1(demultiplexer_4_out1), .in({2{write}}), .sel(Addres[1]));
  Multiplexer #(.select(2), .width(32), .enable("false")) multiplexer_1 (
    .in0(Data), .in1({demultiplexer_2_out1, demultiplexer_2_out0}),
    .in2({demultiplexer_3_out3, demultiplexer_3_out2, demultiplexer_3_out1, demultiplexer_3_out0}),
    .out(multiplexer_1_out), .sel(whb));  // open: in3
  Multiplexer #(.select(2), .width(4), .enable("false")) multiplexer_2 (
    .in0({4{write}}), .in1({demultiplexer_4_out1, demultiplexer_4_out0}), .in2(demultiplexer_1_out0),
    .out(multiplexer_2_out), .sel(whb));  // open: in3
  RAM #(.addrWidth(24), .databus("bibus")) ram_1 (
    .addr(Addres[25:2]), .we(multiplexer_2_out[0]), .oe(read), .clk(clk), .din(multiplexer_1_out[7:0]),
    .dout(ram_1_dout));
  RAM #(.addrWidth(24), .databus("bibus")) ram_2 (
    .addr(Addres[25:2]), .we(multiplexer_2_out[1]), .oe(read), .clk(clk), .din(multiplexer_1_out[15:8]),
    .dout(ram_2_dout));
  RAM #(.addrWidth(24), .databus("bibus")) ram_3 (
    .addr(Addres[25:2]), .we(multiplexer_2_out[2]), .oe(read), .clk(clk), .din(multiplexer_1_out[23:16]),
    .dout(ram_3_dout));
  RAM #(.addrWidth(24), .databus("bibus")) ram_4 (
    .addr(Addres[25:2]), .we(multiplexer_2_out[3]), .oe(read), .clk(clk), .din(multiplexer_1_out[31:24]),
    .dout(ram_4_dout));
  Multiplexer #(.width(16), .enable("false")) multiplexer_3 (
    .in0({ram_2_dout, ram_1_dout}), .in1({ram_4_dout, ram_3_dout}), .out(multiplexer_3_out), .sel(Addres[1]));
  Multiplexer #(.select(2), .width(8), .enable("false")) multiplexer_4 (
    .in0(ram_1_dout), .in1(ram_2_dout), .in2(ram_3_dout), .in3(ram_4_dout), .out(multiplexer_4_out),
    .sel(Addres[1:0]));
  Multiplexer #(.select(2), .width(32), .enable("false")) multiplexer_5 (
    .in0({ram_4_dout, ram_3_dout, ram_2_dout, ram_1_dout}), .in1({{16{1'b0}}, multiplexer_3_out}),
    .in2({{24{1'b0}}, multiplexer_4_out}), .out(Read_Data), .sel(whb));  // open: in3
endmodule

module circuito_de_busca (
  input  [31:0] Next_PC,
  input  Write,
  input  clk,
  output [31:0] PC_4,
  output [31:0] instruction
);

  wire [23:0] register_1_q_2;
  wire [31:0] register_1_q;

  Register #(.width(32)) register_1 (
    .D(Next_PC), .en(Write), .clk(clk), .Q({register_1_q[31:26], register_1_q_2, register_1_q[1:0]}),
    .clr(1'b0));
  Adder #(.width(32)) adder_1 (
    .a({register_1_q[31:26], register_1_q_2, register_1_q[1:0]}), .b(32'h4), .out(PC_4), .cin(1'b0));  // open: cout
  ROM #(.addrWidth(24), .dataWidth(32)) rom_1 (.addr(register_1_q_2), .data(instruction));
endmodule

module signalExtend (
  input  [15:0] SignalXIn,
  output [31:0] signalXOut
);


  assign signalXOut = {{17{SignalXIn[15]}}, SignalXIn[14:0]};
endmodule

module Shift2 (
  input  [31:0] ShiftIn,
  output [31:0] ShiftOut
);


  assign ShiftOut = {ShiftIn[29:0], 2'b00};
endmodule
